// Logisim project 3bc.circ as structural Verilog: 2 circuits, main circuit main
module a (
  input  CLK,
  input  RST,
  output Q3,
  output Q1,
  output Q2
);

  wire n7408_1_pin6, n74283_1_pin2;

  _7408 u_7408_1 (
    .pin4(Q2), .pin5(Q3), .pin6(n7408_1_pin6));  // open: pin1, pin2, pin3, pin13, pin12, pin11, pin10, pin9, pin8
  _74283 u_74283_1 (
    .pin1(CLK), .pin2(n74283_1_pin2), .pin3(n74283_1_pin2), .pin5(Q3), .pin15(RST), .pin14(RST), .pin13(CLK),
    .pin12(n7408_1_pin6), .pin11(n7408_1_pin6), .pin9(Q1));  // open: pin4, pin6, pin7, pin10
  _74283 u_74283_2 (
    .pin1(CLK), .pin2(Q3), .pin3(Q3), .pin5(Q2), .pin15(RST));  // open: pin4, pin6, pin7, pin14, pin13, pin12, pin11, pin10, pin9
  // also tied to VCC on the sheet: n74283_1_pin2
endmodule

module main (
  input  in_1,
  input  CLK,
  output Q3,
  output Q2,
  output out_5
);

  wire n7408_1_pin6, n74283_1_pin12, n74283_2_pin2, n74283_2_pin5, n74283_2_pin12;

  _7408 u_7408_1 (
    .pin4(Q3), .pin5(Q2), .pin6(n7408_1_pin6));  // open: pin1, pin2, pin3, pin13, pin12, pin11, pin10, pin9, pin8
  _74283 u_74283_1 (
    .pin1(CLK), .pin2(n7408_1_pin6), .pin3(n7408_1_pin6), .pin5(Q3), .pin13(CLK), .pin12(n74283_1_pin12),
    .pin11(n74283_1_pin12), .pin9(Q2));  // open: pin4, pin6, pin7, pin15, pin14, pin10
  _74283 u_74283_2 (
    .pin1(CLK), .pin2(n74283_2_pin2), .pin3(n74283_2_pin2), .pin5(n74283_2_pin5), .pin13(CLK),
    .pin12(n74283_2_pin12), .pin11(n74283_2_pin12));  // open: pin4, pin6, pin7, pin15, pin14, pin10, pin9
endmodule
