// Logisim project tictac1.circ as structural Verilog: 12 circuits, main circuit master
module main (
  input  Reset,
  input  LTi,
  input  MTi,
  input  RTi,
  input  LMi,
  input  MMi,
  input  RMi,
  input  LBi,
  input  MBi,
  input  RBi,
  output LTo0,
  output LMo0,
  output LBo0,
  output LTo1,
  output LMo1,
  output LBo1,
  output MTo0,
  output MMo0,
  output MBo0,
  output MTo1,
  output MMo1,
  output MBo1,
  output RTo0,
  output RMo0,
  output RBo0,
  output RTo1,
  output RMo1,
  output RBo1,
  output Turn
);

  wire memory_1_change, memory_2_change, memory_3_change, memory_4_change, memory_5_change, memory_6_change,
       memory_7_change, memory_8_change, memory_9_change, or_1_out;

  Memory memory_1 (.Write(LTi), .Turn(Turn), .Reset(Reset), .C0(LTo0), .C1(LTo1), .Change(memory_1_change));
  Memory memory_2 (.Write(MTi), .Turn(Turn), .Reset(Reset), .C0(MTo0), .C1(MTo1), .Change(memory_2_change));
  Memory memory_3 (.Write(RTi), .Turn(Turn), .Reset(Reset), .C0(RTo0), .C1(RTo1), .Change(memory_3_change));
  T_Flip_Flop t_ff_1 (.T(or_1_out), .clk(or_1_out), .Q(Turn));  // open: Qn, reset, preset
  or or_1 (or_1_out, memory_1_change, memory_2_change, memory_3_change, memory_4_change, memory_5_change, memory_6_change, memory_7_change, memory_8_change, memory_9_change);
  Memory memory_4 (.Write(LMi), .Turn(Turn), .Reset(Reset), .C0(LMo0), .C1(LMo1), .Change(memory_4_change));
  Memory memory_5 (.Write(MMi), .Turn(Turn), .Reset(Reset), .C0(MMo0), .C1(MMo1), .Change(memory_5_change));
  Memory memory_6 (.Write(RMi), .Turn(Turn), .Reset(Reset), .C0(RMo0), .C1(RMo1), .Change(memory_6_change));
  Memory memory_7 (.Write(LBi), .Turn(Turn), .Reset(Reset), .C0(LBo0), .C1(LBo1), .Change(memory_7_change));
  Memory memory_8 (.Write(MBi), .Turn(Turn), .Reset(Reset), .C0(MBo0), .C1(MBo1), .Change(memory_8_change));
  Memory memory_9 (.Write(RBi), .Turn(Turn), .Reset(Reset), .C0(RBo0), .C1(RBo1), .Change(memory_9_change));
endmodule

module winDetector (
  input  A1,
  input  A0,
  input  B1,
  input  B0,
  input  C1,
  input  in_6,
  output out_7
);

  wire and_1_out, and_2_out, nor_1_out, or_1_out;

  and and_1 (and_1_out, A1, B1, C1);
  and and_2 (and_2_out, A0, B0, in_6);
  nor nor_1 (nor_1_out, A0, B0, in_6);
  or or_1 (or_1_out, and_2_out, nor_1_out);
  and and_3 (out_7, and_1_out, or_1_out);
endmodule

module master (
);

  wire button_1_out, button_2_out, button_3_out, button_4_out, button_5_out, button_6_out, button_7_out,
       button_8_out, button_9_out, button_10_out, gridmemory_1_lbo0, gridmemory_1_lbo1, gridmemory_1_lmo0,
       gridmemory_1_lmo1, gridmemory_1_lto0, gridmemory_1_lto1, gridmemory_1_mbo0, gridmemory_1_mbo1,
       gridmemory_1_mmo0, gridmemory_1_mmo1, gridmemory_1_mto0, gridmemory_1_mto1, gridmemory_1_rbo0,
       gridmemory_1_rbo1, gridmemory_1_rmo0, gridmemory_1_rmo1, gridmemory_1_rto0, gridmemory_1_rto1,
       LB_center, LB_corners, LB_cross, LM_center, LM_corners, LM_cross, LT_center, LT_corners, LT_cross,
       MBd_center, MBd_corners, MBd_cross, MMd_center, MMd_corners, MMd_cross, MT_center, MT_corners,
       MT_cross, RBd_center, RBd_corners, RBd_cross, RMd_center, RMd_corners, RMd_cross, RTd_center,
       RTd_corners, RTd_cross;

  Button button_1 (.out(button_1_out));
  Button button_2 (.out(button_2_out));
  Button button_3 (.out(button_3_out));
  Button button_4 (.out(button_4_out));
  Button button_5 (.out(button_5_out));
  Button button_6 (.out(button_6_out));
  Button button_7 (.out(button_7_out));
  Button button_8 (.out(button_8_out));
  Button button_9 (.out(button_9_out));
  Button button_10 (.out(button_10_out));
  GridMemory gridmemory_1 (
    .Reset(button_1_out), .LTi(button_2_out), .MTi(button_5_out), .RTi(button_6_out), .LMi(button_3_out),
    .MMi(button_7_out), .RMi(button_8_out), .LBi(button_4_out), .MBi(button_9_out), .RBi(button_10_out),
    .LTo0(gridmemory_1_lto0), .LMo0(gridmemory_1_lmo0), .LBo0(gridmemory_1_lbo0), .LTo1(gridmemory_1_lto1),
    .LMo1(gridmemory_1_lmo1), .LBo1(gridmemory_1_lbo1), .MTo0(gridmemory_1_mto0), .MMo0(gridmemory_1_mmo0),
    .MBo0(gridmemory_1_mbo0), .MTo1(gridmemory_1_mto1), .MMo1(gridmemory_1_mmo1), .MBo1(gridmemory_1_mbo1),
    .RTo0(gridmemory_1_rto0), .RMo0(gridmemory_1_rmo0), .RBo0(gridmemory_1_rbo0), .RTo1(gridmemory_1_rto1),
    .RMo1(gridmemory_1_rmo1), .RBo1(gridmemory_1_rbo1));  // open: Turn
  winDetector windetector_1 ();  // open: A1, A0, B1, B0, C1, in_6, out_7
  Display LT (
    .C0(gridmemory_1_lto0), .C1(gridmemory_1_lto1), .Corners(LT_corners), .Center(LT_center), .Cross(LT_cross));
  Display LM (
    .C0(gridmemory_1_lmo0), .C1(gridmemory_1_lmo1), .Corners(LM_corners), .Center(LM_center), .Cross(LM_cross));
  Display LB (
    .C0(gridmemory_1_lbo0), .C1(gridmemory_1_lbo1), .Corners(LB_corners), .Center(LB_center), .Cross(LB_cross));
  LED led_1 (.in(LT_corners));
  LED led_2 (.in(LT_cross));
  LED led_3 (.in(LT_corners));
  LED led_4 (.in(LT_center));
  LED led_5 (.in(LT_cross));
  LED led_6 (.in(LT_cross));
  LED led_7 (.in(LT_corners));
  LED led_8 (.in(LT_cross));
  LED led_9 (.in(LT_corners));
  LED led_10 (.in(LM_corners));
  LED led_11 (.in(LM_cross));
  LED led_12 (.in(LM_corners));
  LED led_13 (.in(LM_center));
  LED led_14 (.in(LM_cross));
  LED led_15 (.in(LM_cross));
  LED led_16 (.in(LM_corners));
  LED led_17 (.in(LM_cross));
  LED led_18 (.in(LM_corners));
  LED led_19 (.in(LB_corners));
  LED led_20 (.in(LB_cross));
  LED led_21 (.in(LB_corners));
  LED led_22 (.in(LB_center));
  LED led_23 (.in(LB_cross));
  LED led_24 (.in(LB_cross));
  LED led_25 (.in(LB_corners));
  LED led_26 (.in(LB_cross));
  LED led_27 (.in(LB_corners));
  Display MT (
    .C0(gridmemory_1_mto0), .C1(gridmemory_1_mto1), .Corners(MT_corners), .Center(MT_center), .Cross(MT_cross));
  Display MMd (
    .C0(gridmemory_1_mmo0), .C1(gridmemory_1_mmo1), .Corners(MMd_corners), .Center(MMd_center),
    .Cross(MMd_cross));
  Display MBd (
    .C0(gridmemory_1_mbo0), .C1(gridmemory_1_mbo1), .Corners(MBd_corners), .Center(MBd_center),
    .Cross(MBd_cross));
  LED led_28 (.in(MT_corners));
  LED led_29 (.in(MT_cross));
  LED led_30 (.in(MT_corners));
  LED led_31 (.in(MT_center));
  LED led_32 (.in(MT_cross));
  LED led_33 (.in(MT_cross));
  LED led_34 (.in(MT_corners));
  LED led_35 (.in(MT_cross));
  LED led_36 (.in(MT_corners));
  LED led_37 (.in(MMd_corners));
  LED led_38 (.in(MMd_cross));
  LED led_39 (.in(MMd_corners));
  LED led_40 (.in(MMd_center));
  LED led_41 (.in(MMd_cross));
  LED led_42 (.in(MMd_cross));
  LED led_43 (.in(MMd_corners));
  LED led_44 (.in(MMd_cross));
  LED led_45 (.in(MMd_corners));
  LED led_46 (.in(MBd_corners));
  LED led_47 (.in(MBd_cross));
  LED led_48 (.in(MBd_corners));
  LED led_49 (.in(MBd_center));
  LED led_50 (.in(MBd_cross));
  LED led_51 (.in(MBd_cross));
  LED led_52 (.in(MBd_corners));
  LED led_53 (.in(MBd_cross));
  LED led_54 (.in(MBd_corners));
  LED led_55 (.in(RTd_corners));
  Display RTd (
    .C0(gridmemory_1_rto0), .C1(gridmemory_1_rto1), .Corners(RTd_corners), .Center(RTd_center),
    .Cross(RTd_cross));
  LED led_56 (.in(RTd_cross));
  LED led_57 (.in(RTd_corners));
  LED led_58 (.in(RMd_corners));
  Display RMd (
    .C0(gridmemory_1_rmo0), .C1(gridmemory_1_rmo1), .Corners(RMd_corners), .Center(RMd_center),
    .Cross(RMd_cross));
  LED led_59 (.in(RMd_cross));
  LED led_60 (.in(RMd_corners));
  LED led_61 (.in(RBd_corners));
  Display RBd (
    .C0(gridmemory_1_rbo0), .C1(gridmemory_1_rbo1), .Corners(RBd_corners), .Center(RBd_center),
    .Cross(RBd_cross));
  LED led_62 (.in(RBd_cross));
  LED led_63 (.in(RBd_corners));
  LED led_64 (.in(RTd_cross));
  LED led_65 (.in(RTd_corners));
  LED led_66 (.in(RTd_center));
  LED led_67 (.in(RTd_cross));
  LED led_68 (.in(RTd_cross));
  LED led_69 (.in(RTd_corners));
  LED led_70 (.in(RMd_cross));
  LED led_71 (.in(RMd_corners));
  LED led_72 (.in(RMd_center));
  LED led_73 (.in(RMd_cross));
  LED led_74 (.in(RMd_cross));
  LED led_75 (.in(RMd_corners));
  LED led_76 (.in(RBd_cross));
  LED led_77 (.in(RBd_corners));
  LED led_78 (.in(RBd_center));
  LED led_79 (.in(RBd_cross));
  LED led_80 (.in(RBd_cross));
  LED led_81 (.in(RBd_corners));
endmodule

module Display (
  input  C0,
  input  C1,
  output Corners,
  output Center,
  output Cross
);

  wire not_1_out;

  not not_1 (not_1_out, C1);
  and and_1 (Center, C0, C1);
  and and_2 (Cross, C0, not_1_out);

  assign Corners = C0;
endmodule

module Memory (
  input  Write,
  input  Turn,
  input  Reset,
  output C0,
  output C1,
  output Change
);

  wire and_1_out, not_1_out, s_r_ff_1_qn;

  and and_1 (and_1_out, s_r_ff_1_qn, Write, Turn);
  S_R_Flip_Flop #(.trigger("low")) s_r_ff_1 (
    .S(Write), .R(Reset), .clk(1'b0), .Q(C0), .Qn(s_r_ff_1_qn));  // open: reset, preset
  S_R_Flip_Flop #(.trigger("low")) s_r_ff_2 (.S(and_1_out), .R(Reset), .clk(1'b0), .Q(C1));  // open: reset, Qn, preset
  and and_2 (Change, C0, not_1_out);
  not not_1 (not_1_out, C0);
endmodule

module GridMemory (
  input  Reset,
  input  LTi,
  input  MTi,
  input  RTi,
  input  LMi,
  input  MMi,
  input  RMi,
  input  LBi,
  input  MBi,
  input  RBi,
  output LTo0,
  output LMo0,
  output LBo0,
  output LTo1,
  output LMo1,
  output LBo1,
  output MTo0,
  output MMo0,
  output MBo0,
  output MTo1,
  output MMo1,
  output MBo1,
  output RTo0,
  output RMo0,
  output RBo0,
  output RTo1,
  output RMo1,
  output RBo1,
  output Turn
);

  wire memory_1_change, memory_2_change, memory_3_change, memory_4_change, memory_5_change, memory_6_change,
       memory_7_change, memory_8_change, memory_9_change, or_1_out;

  Memory memory_1 (.Write(LTi), .Turn(Turn), .Reset(Reset), .C0(LTo0), .C1(LTo1), .Change(memory_1_change));
  Memory memory_2 (.Write(MTi), .Turn(Turn), .Reset(Reset), .C0(MTo0), .C1(MTo1), .Change(memory_2_change));
  Memory memory_3 (.Write(RTi), .Turn(Turn), .Reset(Reset), .C0(RTo0), .C1(RTo1), .Change(memory_3_change));
  T_Flip_Flop t_ff_1 (.T(or_1_out), .clk(or_1_out), .Q(Turn));  // open: Qn, reset, preset
  or or_1 (or_1_out, memory_1_change, memory_2_change, memory_3_change, memory_4_change, memory_5_change, memory_6_change, memory_7_change, memory_8_change, memory_9_change);
  Memory memory_4 (.Write(LMi), .Turn(Turn), .Reset(Reset), .C0(LMo0), .C1(LMo1), .Change(memory_4_change));
  Memory memory_5 (.Write(MMi), .Turn(Turn), .Reset(Reset), .C0(MMo0), .C1(MMo1), .Change(memory_5_change));
  Memory memory_6 (.Write(RMi), .Turn(Turn), .Reset(Reset), .C0(RMo0), .C1(RMo1), .Change(memory_6_change));
  Memory memory_7 (.Write(LBi), .Turn(Turn), .Reset(Reset), .C0(LBo0), .C1(LBo1), .Change(memory_7_change));
  Memory memory_8 (.Write(MBi), .Turn(Turn), .Reset(Reset), .C0(MBo0), .C1(MBo1), .Change(memory_8_change));
  Memory memory_9 (.Write(RBi), .Turn(Turn), .Reset(Reset), .C0(RBo0), .C1(RBo1), .Change(memory_9_change));
endmodule

module dispChip2 (
  input  A1,
  input  E1,
  input  I1,
  input  A0,
  input  E0,
  input  I0,
  input  B1,
  input  F1,
  input  B0,
  input  F0,
  input  C1,
  input  G1,
  input  C0,
  input  G0,
  input  D1,
  input  H1,
  input  D0,
  input  H0,
  output oA,
  output rA,
  output eA,
  output oE,
  output rE,
  output eE,
  output oI,
  output rI,
  output eI,
  output oB,
  output rB,
  output eB,
  output orF,
  output rF,
  output eF,
  output oC,
  output rC,
  output eC,
  output oG,
  output rG,
  output eG,
  output oD,
  output rD,
  output eD,
  output oH,
  output rH,
  output eH
);

  wire n7400_1_pin1, n7400_1_pin13, n7400_3_pin1, n7400_3_pin13, n7400_5_pin1, n7400_5_pin13, n7400_7_pin1,
       n7400_7_pin13, n7400_9_pin13;

  _7400 u_7400_1 (
    .pin1(n7400_1_pin1), .pin2(E1), .pin3(rE), .pin4(E0), .pin5(E1), .pin6(eE), .pin13(n7400_1_pin13),
    .pin12(A1), .pin11(rA), .pin10(A0), .pin9(A1), .pin8(eA));
  _7400 u_7400_2 (
    .pin1(E1), .pin2(E1), .pin3(oE), .pin4(E0), .pin5(E0), .pin6(n7400_1_pin1), .pin13(A1), .pin12(A1),
    .pin11(oA), .pin10(A0), .pin9(A0), .pin8(n7400_1_pin13));
  _7400 u_7400_3 (
    .pin1(n7400_3_pin1), .pin2(F1), .pin3(rF), .pin4(F0), .pin5(F1), .pin6(eF), .pin13(n7400_3_pin13),
    .pin12(B1), .pin11(rB), .pin10(B0), .pin9(B1), .pin8(eB));
  _7400 u_7400_4 (
    .pin1(F1), .pin2(F1), .pin3(orF), .pin4(F0), .pin5(F0), .pin6(n7400_3_pin1), .pin13(B1), .pin12(B1),
    .pin11(oB), .pin10(B0), .pin9(B0), .pin8(n7400_3_pin13));
  _7400 u_7400_5 (
    .pin1(n7400_5_pin1), .pin2(G1), .pin3(rG), .pin4(G0), .pin5(G1), .pin6(eG), .pin13(n7400_5_pin13),
    .pin12(C1), .pin11(rC), .pin10(C0), .pin9(C1), .pin8(eC));
  _7400 u_7400_6 (
    .pin1(G1), .pin2(G1), .pin3(oG), .pin4(G0), .pin5(G0), .pin6(n7400_5_pin1), .pin13(C1), .pin12(C1),
    .pin11(oC), .pin10(C0), .pin9(C0), .pin8(n7400_5_pin13));
  _7400 u_7400_7 (
    .pin1(n7400_7_pin1), .pin2(H1), .pin3(rH), .pin4(H0), .pin5(H1), .pin6(eH), .pin13(n7400_7_pin13),
    .pin12(D1), .pin11(rD), .pin10(D0), .pin9(D1), .pin8(eD));
  _7400 u_7400_8 (
    .pin1(H1), .pin2(H1), .pin3(oH), .pin4(H0), .pin5(H0), .pin6(n7400_7_pin1), .pin13(D1), .pin12(D1),
    .pin11(oD), .pin10(D0), .pin9(D0), .pin8(n7400_7_pin13));
  _7400 u_7400_9 (
    .pin13(n7400_9_pin13), .pin12(I1), .pin11(rI), .pin10(I0), .pin9(I1), .pin8(eI));  // open: pin1, pin2, pin3, pin4, pin5, pin6
  _7400 u_7400_10 (
    .pin13(I1), .pin12(I1), .pin11(oI), .pin10(I0), .pin9(I0), .pin8(n7400_9_pin13));  // open: pin1, pin2, pin3, pin4, pin5, pin6
endmodule

module fsmMem (
  input  W,
  input  T,
  input  CLK,
  input  RST,
  input  CLR,
  input  in_6,
  input  W1,
  input  W2,
  input  W3,
  input  W4,
  input  W5,
  input  W6,
  input  W7,
  input  W8,
  input  W9,
  input  in_16
);

  wire and_1_out, and_2_out, d_ff_1_q, d_ff_2_q, not_1_out, or_1_out, or_2_out;

  not not_1 (not_1_out, d_ff_1_q);
  and and_1 (and_1_out, W, not_1_out);
  and and_2 (and_2_out, not_1_out, T, W);
  // NOT_Gate not_2 has open pins: in=CLR, out=open
  or or_1 (or_1_out, d_ff_1_q, and_1_out);
  or or_2 (or_2_out, d_ff_2_q, and_2_out);
  D_Flip_Flop d_ff_1 (.D(or_1_out), .clk(CLK), .Q(d_ff_1_q), .reset(RST));  // open: Qn, preset
  D_Flip_Flop d_ff_2 (.D(or_2_out), .clk(CLK), .Q(d_ff_2_q), .reset(RST));  // open: Qn, preset
endmodule

module memchip (
  input  CLR,
  input  T,
  input  W1,
  input  W2,
  input  W3,
  input  W4,
  input  W5,
  input  W6,
  input  W7,
  input  W8,
  input  W9,
  input  CLK
);

  wire n7404_1_pin5, n7404_1_pin6, n7408_1_pin3, n7408_1_pin6, n7432_1_pin2, n7432_1_pin3, n7432_1_pin6,
       not_1_out;

  not not_1 (not_1_out, CLR);
  _7404 u_7404_1 (
    .pin5(n7404_1_pin5), .pin6(n7404_1_pin6));  // open: pin1, pin2, pin3, pin4, pin13, pin12, pin11, pin10, pin9, pin8
  _7408 u_7408_1 (
    .pin1(n7404_1_pin6), .pin2(W1), .pin3(n7408_1_pin3), .pin4(n7408_1_pin3), .pin5(T), .pin6(n7408_1_pin6));  // open: pin13, pin12, pin11, pin10, pin9, pin8
  _7432 u_7432_1 (
    .pin1(n7408_1_pin6), .pin2(n7432_1_pin2), .pin3(n7432_1_pin3), .pin4(W1), .pin5(n7404_1_pin5),
    .pin6(n7432_1_pin6));  // open: pin13, pin12, pin11, pin10, pin9, pin8
  _74273 u_74273_1 (
    .pin1(not_1_out), .pin2(n7404_1_pin5), .pin3(n7432_1_pin6), .pin4(n7432_1_pin3), .pin5(n7432_1_pin2),
    .pin11(CLK));  // open: pin6, pin7, pin8, pin9, pin19, pin18, pin17, pin16, pin15, pin14, pin13, pin12
endmodule

module WinChip (
  input  A1,
  input  A0,
  input  B1,
  input  B0,
  input  C1,
  input  C0,
  input  D1,
  input  D0,
  input  E1,
  input  E0,
  input  F1,
  input  F0,
  input  G1,
  input  G0,
  input  H1,
  input  H0,
  input  I1,
  input  I0,
  output Win1
);

  wire n7411_1_pin6, n7411_1_pin8, n7411_1_pin9, n7411_1_pin10, n7411_1_pin11, n7411_1_pin12, n7432_1_pin3;

  _7411 u_7411_1 (
    .pin1(B0), .pin2(C0), .pin3(A1), .pin4(B1), .pin5(C1), .pin6(n7411_1_pin6), .pin13(A0),
    .pin12(n7411_1_pin12), .pin11(n7411_1_pin11), .pin10(n7411_1_pin10), .pin9(n7411_1_pin9),
    .pin8(n7411_1_pin8));
  _7404 u_7404_1 (
    .pin1(C0), .pin2(n7411_1_pin11), .pin3(B0), .pin4(n7411_1_pin10), .pin5(A0), .pin6(n7411_1_pin9));  // open: pin13, pin12, pin11, pin10, pin9, pin8
  _7432 u_7432_1 (
    .pin1(n7411_1_pin12), .pin2(n7411_1_pin8), .pin3(n7432_1_pin3));  // open: pin4, pin5, pin6, pin13, pin12, pin11, pin10, pin9, pin8
  _7408 u_7408_1 (
    .pin1(n7432_1_pin3), .pin2(n7411_1_pin6), .pin3(Win1));  // open: pin4, pin5, pin6, pin13, pin12, pin11, pin10, pin9, pin8
endmodule

module windc2 (
  input  A1,
  input  A0,
  input  B1,
  input  B0,
  input  C1,
  input  C0,
  input  D1,
  input  D0,
  input  E1,
  input  E0,
  input  F1,
  input  F0,
  input  G1,
  input  G0,
  input  H1,
  input  H0,
  input  I1,
  input  I0
);

  wire ROW_OCC_pin6, ROW_OCC_pin8;

  _7411 ROW_OCC (
    .pin1(E1), .pin2(F1), .pin3(G1), .pin4(H1), .pin5(I1), .pin6(ROW_OCC_pin6), .pin13(D1), .pin11(C1),
    .pin10(B1), .pin9(A1), .pin8(ROW_OCC_pin8));  // open: pin12
  _7411 COL_OCC (
    .pin1(H1), .pin2(E1), .pin3(C1), .pin4(I1), .pin5(F1), .pin13(B1), .pin11(G1), .pin10(A1), .pin9(D1));  // open: pin6, pin12, pin8
  _7411 DIA_OCC (
    .pin3(C1), .pin4(G1), .pin5(E1), .pin11(I1), .pin10(E1), .pin9(A1));  // open: pin1, pin2, pin6, pin13, pin12, pin8
  _7411 u_7411_1 ();  // open: pin1, pin2, pin3, pin4, pin5, pin6, pin13, pin12, pin11, pin10, pin9, pin8
endmodule

module memChip2 (
  input  Ta,
  input  Wc,
  input  C1,
  input  D1,
  input  E1,
  input  F1,
  input  Wa,
  input  Wb,
  input  nCLR,
  input  CLK,
  input  Wd,
  input  We,
  input  Wf,
  output B0,
  output B1,
  output A1,
  output A0,
  output WB0,
  output WA1,
  output WF1,
  output WF0,
  output WA0
);

  wire n7404_1_pin8, n7404_1_pin10, n7404_1_pin12, n7404_2_pin8, n7404_2_pin10, n7404_2_pin12, n7411_1_pin3,
       n7411_1_pin6, n7411_1_pin8, n7411_1_pin11, n7411_1_pin12, n7411_1_pin13, n7411_2_pin6, n7411_2_pin8,
       n7411_2_pin12, n7411_3_pin8, n7432_1_pin11, n7432_2_pin6, n7432_2_pin8, n7432_3_pin3, n7432_3_pin8,
       n74273_1_pin14;

  _74273 u_74273_1 (
    .pin1(nCLR), .pin19(A1), .pin18(WA1), .pin17(WA0), .pin16(A0), .pin15(B1), .pin14(n74273_1_pin14),
    .pin13(WB0), .pin12(B0), .pin11(CLK));  // open: pin2, pin3, pin4, pin5, pin6, pin7, pin8, pin9
  _7411 u_7411_1 (
    .pin1(Ta), .pin2(Wa), .pin3(n7411_1_pin3), .pin4(Ta), .pin5(Wb), .pin6(n7411_1_pin6),
    .pin13(n7411_1_pin13), .pin12(n7411_1_pin12), .pin11(n7411_1_pin11), .pin10(Ta), .pin9(Wc),
    .pin8(n7411_1_pin8));
  _7432 u_7432_1 (
    .pin1(n7411_1_pin6), .pin2(B0), .pin3(WB0), .pin4(A1), .pin5(Wa), .pin6(WA1), .pin13(n7411_1_pin8),
    .pin11(n7432_1_pin11), .pin10(B1), .pin9(Wb), .pin8(n74273_1_pin14));  // open: pin12
  _7404 u_7404_1 (
    .pin1(A1), .pin2(n7411_1_pin13), .pin3(C1), .pin4(n7411_1_pin11), .pin5(B1), .pin6(n7411_1_pin3),
    .pin13(E1), .pin12(n7404_1_pin12), .pin11(D1), .pin10(n7404_1_pin10), .pin9(F1), .pin8(n7404_1_pin8));
  _7432 u_7432_2 (
    .pin1(A0), .pin2(n7411_1_pin12), .pin3(WA0), .pin4(C1), .pin5(Wc), .pin6(n7432_2_pin6), .pin10(We),
    .pin9(E1), .pin8(n7432_2_pin8));  // open: pin13, pin12, pin11
  _7411 u_7411_2 (
    .pin1(We), .pin2(n7404_1_pin12), .pin3(Ta), .pin4(Wd), .pin5(n7404_1_pin10), .pin6(n7411_2_pin6),
    .pin13(Ta), .pin12(n7411_2_pin12), .pin11(Ta), .pin10(Wf), .pin9(n7404_1_pin8), .pin8(n7411_2_pin8));
  _7432 u_7432_3 (
    .pin1(n7411_2_pin6), .pin3(n7432_3_pin3), .pin4(Wf), .pin5(F1), .pin6(WF1), .pin13(n7411_2_pin8),
    .pin11(WF0), .pin10(n7411_2_pin12), .pin8(n7432_3_pin8));  // open: pin2, pin12, pin9
  _74273 u_74273_2 ();  // open: pin1, pin2, pin3, pin4, pin5, pin6, pin7, pin8, pin9, pin19, pin18, pin17, pin16, pin15, pin14, pin13, pin12, pin11
  _7404 u_7404_2 (
    .pin12(n7404_2_pin12), .pin10(n7404_2_pin10), .pin8(n7404_2_pin8));  // open: pin1, pin2, pin3, pin4, pin5, pin6, pin13, pin11, pin9
  _7432 u_7432_4 ();  // open: pin1, pin2, pin3, pin4, pin5, pin6, pin13, pin12, pin11, pin10, pin9, pin8
  _74273 u_74273_3 ();  // open: pin1, pin2, pin3, pin4, pin5, pin6, pin7, pin8, pin9, pin19, pin18, pin17, pin16, pin15, pin14, pin13, pin12, pin11
  _7411 u_7411_3 (
    .pin1(n7404_2_pin12), .pin5(n7404_2_pin10), .pin9(n7404_2_pin8), .pin8(n7411_3_pin8));  // open: pin2, pin3, pin4, pin6, pin13, pin12, pin11, pin10
  _7432 u_7432_5 ();  // open: pin1, pin2, pin3, pin4, pin5, pin6, pin13, pin12, pin11, pin10, pin9, pin8
endmodule
